# Fritzing sketch Schema elettrico (saved by Fritzing 0.9.3b)
breadboards: 1

parts:
  Arduino_nano_i2c_sensori = Arduino Nano (Rev3.0)
  Arduino_Nano_i2c_ev3 = Arduino Nano (Rev3.0)
  J1 = female pin header, 4 pins [form="♀ (female)"]
  R1 = Resistor [tolerance=±5% resistance=220 package=THT]
  R2 = Resistor [tolerance=±5% resistance=220 package=THT]
  LED1 = LED - 5mm [color="Red (633nm)" package="5 mm [THT]"]
  LED2 = LED - 5mm [color="Red (633nm)" package="5 mm [THT]"]
  S3 = Pushbutton [package=THT]
  SW1 = DIP SWITCH [package=dipswitch-02]
  J2 = female pin header, 4 pins [form="♀ (female)"]
  J3 = female pin header, 8 pins [form="♀ (female)"]

nets:
  N1: Arduino_nano_i2c_sensori.D1/TX, SW1.1
  N2: Arduino_nano_i2c_sensori.D0/RX, SW1.2
  N3: Arduino_nano_i2c_sensori.RESET, Arduino_Nano_i2c_ev3.RESET, S3.leg1
  GND: Arduino_nano_i2c_sensori.GND, Arduino_Nano_i2c_ev3.GND, J1.pin3, LED1.cathode, LED2.cathode, S3.leg0, J2.pin2
  N4: Arduino_nano_i2c_sensori.D2, J3.pin8
  N5: Arduino_nano_i2c_sensori.D3, J3.pin7
  N6: Arduino_nano_i2c_sensori.D4, J3.pin6
  N7: Arduino_nano_i2c_sensori.D5, J3.pin5
  N8: Arduino_nano_i2c_sensori.D6, J3.pin4
  N9: Arduino_nano_i2c_sensori.D7, J3.pin3
  N10: Arduino_nano_i2c_sensori.D8, J3.pin2
  N11: Arduino_nano_i2c_sensori.D9, J3.pin1
  N12: Arduino_nano_i2c_sensori.D12/MISO, R1.Pin_0
  N13: Arduino_nano_i2c_sensori.A5, J2.pin3
  N14: Arduino_nano_i2c_sensori.A4, J2.pin4
  N15: Arduino_nano_i2c_sensori.3V3, J2.pin1
  N16: Arduino_Nano_i2c_ev3.D1/TX, SW1.3
  N17: Arduino_Nano_i2c_ev3.D0/RX, SW1.4
  N18: Arduino_Nano_i2c_ev3.D12/MISO, R2.Pin_0
  N19: Arduino_Nano_i2c_ev3.VIN, J1.pin4
  N20: Arduino_Nano_i2c_ev3.A5, J1.pin1
  N21: Arduino_Nano_i2c_ev3.A4, J1.pin2
  N22: R1.Pin_1, LED2.anode
  N23: R2.Pin_1, LED1.anode

notes:
  Schema elettrico, Schema elettrico slave
